# Fritzing sketch Wiring-notifyReachedOfficeDeviceNodeMCU (saved by Fritzing 1.0.8)
breadboards: 1

parts:
  U2 = NodeMCU V1.0
  J1 = Piezo Speaker
  LED1 = smd LED [color="Red (633nm)" package="0603 [SMD]"]
  LED2 = smd LED [color="Green (555nm)" package="0603 [SMD]"]

nets:
  N1: U2.D3, J1.pin2
  N2: U2.GND, J1.pin1, LED1.cathode, LED2.cathode
  N3: U2.D7, LED2.anode
  N4: U2.D8, LED1.anode

custom parts:
  NodeMCU V1.0: ESP8266 based NodeMCU
